// Logisim project all project.circ as structural Verilog: 3 circuits, main circuit main
module main (
);

  wire and_1_out, and_2_out, and_3_out, and_4_out, and_5_out, and_6_out, and_7_out, and_8_out, and_9_out,
       and_10_out, and_11_out, and_12_out, and_13_out, and_14_out, and_15_out, and_16_out, and_17_out,
       and_18_out, clock_1_out, d_ff_1_q, d_ff_1_qn, d_ff_2_q, d_ff_2_qn, d_ff_3_q, d_ff_3_qn, d_ff_4_q,
       d_ff_4_qn, d_ff_5_q, d_ff_5_qn, n7404_1_pin4, n7404_2_pin4, n7404_3_pin4, n7404_4_pin4, n7408_1_pin1,
       n7408_1_pin2, n7408_1_pin3, n7408_1_pin4, n7408_1_pin5, n7408_1_pin6, n7408_1_pin8, n7408_1_pin11,
       n7408_1_pin12, n7408_2_pin3, n7408_3_pin3, n7408_3_pin6, n7408_3_pin8, n7408_3_pin11, n7408_4_pin3,
       n7408_5_pin3, n7408_5_pin6, n7408_5_pin8, n7408_5_pin11, n7408_6_pin3, n7408_7_pin3, n7408_7_pin6,
       n7408_7_pin8, n7408_7_pin11, n7408_8_pin3, n7474_1_pin1, n7474_1_pin3, n7474_1_pin9, n7474_2_pin1,
       n7474_2_pin2, n7474_2_pin9, n7486_1_pin3, n7486_1_pin6, n7486_2_pin3, n7486_2_pin6, n7486_3_pin3,
       n7486_3_pin6, n7486_4_pin3, n7486_4_pin6, not_1_out, not_2_out, not_3_out, not_4_out, not_5_out,
       not_6_out, not_7_out, not_8_out, not_9_out, not_10_out, not_11_out, not_12_out, not_13_out,
       not_14_out, not_15_out, not_16_out, not_17_out, not_18_out, not_19_out, not_20_out, not_21_out,
       not_22_out, not_23_out, not_24_out, not_25_out, not_26_out, not_27_out, not_28_out, not_29_out,
       not_30_out, not_31_out, not_32_out, not_33_out, not_34_out, not_35_out, not_36_out, not_37_out,
       not_38_out, not_39_out, not_40_out, not_41_out, not_42_out, not_43_out, not_44_out;

  _7408 u_7408_1 (
    .pin1(n7408_1_pin1), .pin2(n7408_1_pin2), .pin3(n7408_1_pin3), .pin4(n7408_1_pin4), .pin5(n7408_1_pin5),
    .pin6(n7408_1_pin6), .pin13(n7408_1_pin6), .pin12(n7408_1_pin12), .pin11(n7408_1_pin11),
    .pin10(n7408_1_pin6), .pin9(n7408_1_pin3), .pin8(n7408_1_pin8));
  _7474 u_7474_1 (
    .pin1(n7474_1_pin1), .pin2(n7408_1_pin12), .pin3(n7474_1_pin3), .pin4(n7474_1_pin1), .pin5(n7408_1_pin1),
    .pin6(n7408_1_pin12), .pin13(n7474_1_pin1), .pin12(n7408_1_pin2), .pin11(n7408_1_pin12),
    .pin10(n7474_1_pin1), .pin9(n7474_1_pin9), .pin8(n7408_1_pin2));
  Clock clock_1 (.out(clock_1_out));
  _7486 u_7486_1 (
    .pin1(n7408_1_pin1), .pin2(n7474_1_pin9), .pin3(n7486_1_pin3), .pin4(n7408_1_pin1), .pin5(n7474_1_pin9),
    .pin6(n7486_1_pin6));  // open: pin13, pin12, pin11, pin10, pin9, pin8
  D_Flip_Flop d_ff_1 (.D(d_ff_1_qn), .clk(clock_1_out), .Q(d_ff_1_q), .Qn(d_ff_1_qn));  // open: preset, reset
  D_Flip_Flop d_ff_2 (.D(d_ff_2_qn), .clk(d_ff_1_qn), .Q(d_ff_2_q), .Qn(d_ff_2_qn));  // open: preset, reset
  D_Flip_Flop d_ff_3 (.D(d_ff_3_qn), .clk(d_ff_2_qn), .Q(d_ff_3_q), .Qn(d_ff_3_qn));  // open: preset, reset
  D_Flip_Flop d_ff_4 (.D(d_ff_4_qn), .clk(d_ff_3_qn), .Q(d_ff_4_q), .Qn(d_ff_4_qn));  // open: preset, reset
  D_Flip_Flop d_ff_5 (.D(d_ff_5_qn), .clk(d_ff_4_qn), .Q(d_ff_5_q), .Qn(d_ff_5_qn));  // open: preset, reset
  _7474 u_7474_2 (
    .pin1(n7474_2_pin1), .pin2(n7474_2_pin2), .pin3(n7408_1_pin2), .pin4(n7474_2_pin1), .pin5(n7408_1_pin4),
    .pin6(n7474_2_pin2), .pin13(n7474_2_pin1), .pin12(n7408_1_pin5), .pin11(n7474_2_pin2),
    .pin10(n7474_2_pin1), .pin9(n7474_2_pin9), .pin8(n7408_1_pin5));
  _7408 u_7408_2 (
    .pin1(n7486_1_pin6), .pin2(n7408_1_pin6), .pin3(n7408_2_pin3));  // open: pin4, pin5, pin6, pin13, pin12, pin11, pin10, pin9, pin8
  _7404 u_7404_1 (
    .pin1(n7486_1_pin3), .pin3(n7408_2_pin3), .pin4(n7404_1_pin4));  // open: pin2, pin5, pin6, pin13, pin12, pin11, pin10, pin9, pin8
  _7408 u_7408_3 (
    .pin1(n7408_1_pin1), .pin2(n7408_1_pin2), .pin3(n7408_3_pin3), .pin4(n7474_2_pin2), .pin5(n7408_1_pin5),
    .pin6(n7408_3_pin6), .pin13(n7408_3_pin6), .pin12(n7408_1_pin12), .pin11(n7408_3_pin11),
    .pin10(n7408_3_pin6), .pin9(n7408_3_pin3), .pin8(n7408_3_pin8));
  LED led_1 (.in(n7404_1_pin4));
  LED led_2 (.in(n7408_1_pin11));
  LED led_3 (.in(n7408_1_pin8));
  not not_1 (not_1_out, d_ff_2_q);
  not not_2 (not_2_out, d_ff_3_q);
  not not_3 (not_3_out, d_ff_4_q);
  not not_4 (not_4_out, d_ff_5_q);
  not not_5 (not_5_out, d_ff_1_q);
  not not_6 (not_6_out, d_ff_2_q);
  not not_7 (not_7_out, d_ff_4_q);
  not not_8 (not_8_out, d_ff_5_q);
  not not_9 (not_9_out, d_ff_1_q);
  not not_10 (not_10_out, d_ff_4_q);
  not not_11 (not_11_out, d_ff_5_q);
  not not_12 (not_12_out, d_ff_2_q);
  not not_13 (not_13_out, d_ff_4_q);
  not not_14 (not_14_out, d_ff_1_q);
  not not_15 (not_15_out, d_ff_4_q);
  not not_16 (not_16_out, d_ff_5_q);
  not not_17 (not_17_out, d_ff_4_q);
  not not_18 (not_18_out, d_ff_5_q);
  not not_19 (not_19_out, d_ff_1_q);
  not not_20 (not_20_out, d_ff_3_q);
  not not_21 (not_21_out, d_ff_5_q);
  not not_22 (not_22_out, d_ff_3_q);
  not not_23 (not_23_out, d_ff_5_q);
  not not_24 (not_24_out, d_ff_1_q);
  not not_25 (not_25_out, d_ff_2_q);
  not not_26 (not_26_out, d_ff_5_q);
  not not_27 (not_27_out, d_ff_1_q);
  not not_28 (not_28_out, d_ff_1_q);
  not not_29 (not_29_out, d_ff_3_q);
  not not_30 (not_30_out, d_ff_4_q);
  not not_31 (not_31_out, d_ff_1_q);
  not not_32 (not_32_out, d_ff_2_q);
  not not_33 (not_33_out, d_ff_4_q);
  not not_34 (not_34_out, d_ff_2_q);
  not not_35 (not_35_out, d_ff_4_q);
  not not_36 (not_36_out, d_ff_4_q);
  not not_37 (not_37_out, d_ff_2_q);
  not not_38 (not_38_out, d_ff_3_q);
  not not_39 (not_39_out, d_ff_1_q);
  not not_40 (not_40_out, d_ff_3_q);
  _7486 u_7486_2 (
    .pin1(n7408_1_pin1), .pin2(n7474_1_pin9), .pin3(n7486_2_pin3), .pin4(n7408_1_pin1), .pin5(n7474_1_pin9),
    .pin6(n7486_2_pin6));  // open: pin13, pin12, pin11, pin10, pin9, pin8
  _7408 u_7408_4 (
    .pin1(n7486_2_pin6), .pin2(n7408_3_pin6), .pin3(n7408_4_pin3));  // open: pin4, pin5, pin6, pin13, pin12, pin11, pin10, pin9, pin8
  _7404 u_7404_2 (
    .pin1(n7486_2_pin3), .pin3(n7408_4_pin3), .pin4(n7404_2_pin4));  // open: pin2, pin5, pin6, pin13, pin12, pin11, pin10, pin9, pin8
  LED led_4 (.in(n7404_2_pin4));
  LED led_5 (.in(n7408_3_pin11));
  LED led_6 (.in(n7408_3_pin8));
  not not_41 (not_41_out, d_ff_5_q);
  not not_42 (not_42_out, d_ff_3_q);
  not not_43 (not_43_out, d_ff_4_q);
  not not_44 (not_44_out, d_ff_1_q);
  LED led_7 (.in(n7404_3_pin4));
  LED led_8 (.in(n7408_5_pin11));
  LED led_9 (.in(n7408_5_pin8));
  and and_1 (and_1_out, d_ff_1_q, not_1_out, not_2_out, not_3_out, not_4_out);
  and and_2 (and_2_out, not_5_out, not_6_out, d_ff_3_q, not_7_out, not_8_out);
  and and_3 (and_3_out, not_9_out, d_ff_2_q, d_ff_3_q, not_10_out, not_11_out);
  and and_4 (and_4_out, not_14_out, d_ff_2_q, d_ff_3_q, not_15_out, not_16_out);
  and and_5 (and_5_out, d_ff_1_q, d_ff_2_q, d_ff_3_q, not_17_out, not_18_out);
  and and_6 (and_6_out, not_19_out, d_ff_2_q, not_20_out, d_ff_4_q, not_21_out);
  and and_7 (and_7_out, d_ff_1_q, d_ff_2_q, not_22_out, d_ff_4_q, not_23_out);
  and and_8 (and_8_out, not_24_out, not_25_out, d_ff_3_q, d_ff_4_q, not_26_out);
  and and_9 (and_9_out, d_ff_1_q, not_12_out, d_ff_3_q, d_ff_5_q, not_13_out);
  and and_10 (and_10_out, not_27_out, d_ff_2_q, d_ff_3_q, d_ff_4_q, not_41_out);
  and and_11 (and_11_out, d_ff_1_q, d_ff_2_q, d_ff_3_q, d_ff_4_q, d_ff_5_q);
  and and_12 (and_12_out, not_28_out, d_ff_2_q, not_29_out, not_30_out, d_ff_5_q);
  and and_13 (and_13_out, d_ff_1_q, d_ff_2_q, not_42_out, not_43_out, d_ff_5_q);
  and and_14 (and_14_out, not_31_out, not_32_out, d_ff_3_q, not_33_out, d_ff_5_q);
  and and_15 (and_15_out, d_ff_1_q, not_34_out, d_ff_3_q, not_35_out, d_ff_5_q);
  and and_16 (and_16_out, not_44_out, d_ff_2_q, d_ff_3_q, not_36_out, d_ff_5_q);
  and and_17 (and_17_out, d_ff_1_q, not_37_out, not_38_out, d_ff_4_q, d_ff_5_q);
  and and_18 (and_18_out, not_39_out, d_ff_2_q, not_40_out, d_ff_4_q, d_ff_5_q);
  _7408 u_7408_5 (
    .pin1(n7408_1_pin1), .pin2(n7408_1_pin2), .pin3(n7408_5_pin3), .pin4(n7474_2_pin2), .pin5(n7474_2_pin9),
    .pin6(n7408_5_pin6), .pin13(n7408_5_pin6), .pin12(n7408_1_pin12), .pin11(n7408_5_pin11),
    .pin10(n7408_5_pin6), .pin9(n7408_5_pin3), .pin8(n7408_5_pin8));
  LED led_10 (.in(n7404_4_pin4));
  LED led_11 (.in(n7408_7_pin11));
  LED led_12 (.in(n7408_7_pin8));
  _7486 u_7486_3 (
    .pin1(n7408_1_pin1), .pin2(n7474_1_pin9), .pin3(n7486_3_pin3), .pin4(n7408_1_pin1), .pin5(n7474_1_pin9),
    .pin6(n7486_3_pin6));  // open: pin13, pin12, pin11, pin10, pin9, pin8
  _7408 u_7408_6 (
    .pin1(n7486_3_pin6), .pin2(n7408_5_pin6), .pin3(n7408_6_pin3));  // open: pin4, pin5, pin6, pin13, pin12, pin11, pin10, pin9, pin8
  _7404 u_7404_3 (
    .pin1(n7486_3_pin3), .pin3(n7408_6_pin3), .pin4(n7404_3_pin4));  // open: pin2, pin5, pin6, pin13, pin12, pin11, pin10, pin9, pin8
  _7408 u_7408_7 (
    .pin1(n7408_1_pin1), .pin2(n7408_1_pin2), .pin3(n7408_7_pin3), .pin4(n7408_1_pin4), .pin5(n7474_2_pin9),
    .pin6(n7408_7_pin6), .pin13(n7408_7_pin6), .pin12(n7408_1_pin12), .pin11(n7408_7_pin11),
    .pin10(n7408_7_pin6), .pin9(n7408_7_pin3), .pin8(n7408_7_pin8));
  or or_1 (n7474_1_pin3, and_1_out, and_2_out, and_3_out, and_4_out, and_5_out, and_6_out, and_7_out, and_8_out, and_9_out, and_10_out, and_11_out, and_12_out, and_13_out, and_14_out, and_15_out, and_16_out, and_17_out, and_18_out);
  _7486 u_7486_4 (
    .pin1(n7408_1_pin1), .pin2(n7474_1_pin9), .pin3(n7486_4_pin3), .pin4(n7408_1_pin1), .pin5(n7474_1_pin9),
    .pin6(n7486_4_pin6));  // open: pin13, pin12, pin11, pin10, pin9, pin8
  _7408 u_7408_8 (
    .pin1(n7486_4_pin6), .pin2(n7408_7_pin6), .pin3(n7408_8_pin3));  // open: pin4, pin5, pin6, pin13, pin12, pin11, pin10, pin9, pin8
  _7404 u_7404_4 (
    .pin1(n7486_4_pin3), .pin3(n7408_8_pin3), .pin4(n7404_4_pin4));  // open: pin2, pin5, pin6, pin13, pin12, pin11, pin10, pin9, pin8
  // also tied to VCC on the sheet: {n7474_2_pin1, n7474_1_pin1}

  // Notes on the sheet:
  //   1.saniye
  //   4.saniye
  //   5.saniye
  //   6..saniye
  //   7.saniye
  //   10.saniye
  //   11.saniye
  //   12.saniye
  //   13.saniye
  //   14.saniye
  //   15.saniye
  //   18.saniye
  //   19.saniye
  //   20.saniye
  //   21.saniye
  //   22.saniye
  //   25.saniye
  //   26.saniye
endmodule

module selector (
);

  wire clock_1_out, n7404_1_pin4, n7404_2_pin4, n7404_3_pin4, n7404_4_pin4, n7408_1_pin1, n7408_1_pin2,
       n7408_1_pin3, n7408_1_pin4, n7408_1_pin5, n7408_1_pin6, n7408_1_pin8, n7408_1_pin11, n7408_1_pin12,
       n7408_2_pin3, n7408_3_pin3, n7408_3_pin6, n7408_3_pin8, n7408_3_pin11, n7408_4_pin3, n7408_5_pin3,
       n7408_5_pin6, n7408_5_pin8, n7408_5_pin11, n7408_6_pin3, n7408_7_pin3, n7408_7_pin6, n7408_7_pin8,
       n7408_7_pin11, n7408_8_pin3, n7474_1_pin1, n7474_1_pin9, n7474_2_pin1, n7474_2_pin2, n7474_2_pin9,
       n7486_1_pin3, n7486_1_pin6, n7486_2_pin3, n7486_2_pin6, n7486_3_pin3, n7486_3_pin6, n7486_4_pin3,
       n7486_4_pin6;

  _7408 u_7408_1 (
    .pin1(n7408_1_pin1), .pin2(n7408_1_pin2), .pin3(n7408_1_pin3), .pin4(n7408_1_pin4), .pin5(n7408_1_pin5),
    .pin6(n7408_1_pin6), .pin13(n7408_1_pin6), .pin12(n7408_1_pin12), .pin11(n7408_1_pin11),
    .pin10(n7408_1_pin6), .pin9(n7408_1_pin3), .pin8(n7408_1_pin8));
  Clock clock_1 (.out(clock_1_out));
  _7474 u_7474_1 (
    .pin1(n7474_1_pin1), .pin2(n7408_1_pin12), .pin3(clock_1_out), .pin4(n7474_1_pin1), .pin5(n7408_1_pin1),
    .pin6(n7408_1_pin12), .pin13(n7474_1_pin1), .pin12(n7408_1_pin2), .pin11(n7408_1_pin12),
    .pin10(n7474_1_pin1), .pin9(n7474_1_pin9), .pin8(n7408_1_pin2));
  _7486 u_7486_1 (
    .pin1(n7408_1_pin1), .pin2(n7474_1_pin9), .pin3(n7486_1_pin3), .pin4(n7408_1_pin1), .pin5(n7474_1_pin9),
    .pin6(n7486_1_pin6));  // open: pin13, pin12, pin11, pin10, pin9, pin8
  _7474 u_7474_2 (
    .pin1(n7474_2_pin1), .pin2(n7474_2_pin2), .pin3(n7408_1_pin2), .pin4(n7474_2_pin1), .pin5(n7408_1_pin4),
    .pin6(n7474_2_pin2), .pin13(n7474_2_pin1), .pin12(n7408_1_pin5), .pin11(n7474_2_pin2),
    .pin10(n7474_2_pin1), .pin9(n7474_2_pin9), .pin8(n7408_1_pin5));
  _7408 u_7408_2 (
    .pin1(n7486_1_pin6), .pin2(n7408_1_pin6), .pin3(n7408_2_pin3));  // open: pin4, pin5, pin6, pin13, pin12, pin11, pin10, pin9, pin8
  _7404 u_7404_1 (
    .pin1(n7486_1_pin3), .pin3(n7408_2_pin3), .pin4(n7404_1_pin4));  // open: pin2, pin5, pin6, pin13, pin12, pin11, pin10, pin9, pin8
  _7408 u_7408_3 (
    .pin1(n7408_1_pin1), .pin2(n7408_1_pin2), .pin3(n7408_3_pin3), .pin4(n7474_2_pin2), .pin5(n7408_1_pin5),
    .pin6(n7408_3_pin6), .pin13(n7408_3_pin6), .pin12(n7408_1_pin12), .pin11(n7408_3_pin11),
    .pin10(n7408_3_pin6), .pin9(n7408_3_pin3), .pin8(n7408_3_pin8));
  LED led_1 (.in(n7404_1_pin4));
  LED led_2 (.in(n7408_1_pin11));
  LED led_3 (.in(n7408_1_pin8));
  _7486 u_7486_2 (
    .pin1(n7408_1_pin1), .pin2(n7474_1_pin9), .pin3(n7486_2_pin3), .pin4(n7408_1_pin1), .pin5(n7474_1_pin9),
    .pin6(n7486_2_pin6));  // open: pin13, pin12, pin11, pin10, pin9, pin8
  _7408 u_7408_4 (
    .pin1(n7486_2_pin6), .pin2(n7408_3_pin6), .pin3(n7408_4_pin3));  // open: pin4, pin5, pin6, pin13, pin12, pin11, pin10, pin9, pin8
  _7404 u_7404_2 (
    .pin1(n7486_2_pin3), .pin3(n7408_4_pin3), .pin4(n7404_2_pin4));  // open: pin2, pin5, pin6, pin13, pin12, pin11, pin10, pin9, pin8
  LED led_4 (.in(n7404_2_pin4));
  LED led_5 (.in(n7408_3_pin11));
  LED led_6 (.in(n7408_3_pin8));
  LED led_7 (.in(n7404_3_pin4));
  LED led_8 (.in(n7408_5_pin11));
  LED led_9 (.in(n7408_5_pin8));
  _7408 u_7408_5 (
    .pin1(n7408_1_pin1), .pin2(n7408_1_pin2), .pin3(n7408_5_pin3), .pin4(n7474_2_pin2), .pin5(n7474_2_pin9),
    .pin6(n7408_5_pin6), .pin13(n7408_5_pin6), .pin12(n7408_1_pin12), .pin11(n7408_5_pin11),
    .pin10(n7408_5_pin6), .pin9(n7408_5_pin3), .pin8(n7408_5_pin8));
  LED led_10 (.in(n7404_4_pin4));
  LED led_11 (.in(n7408_7_pin11));
  LED led_12 (.in(n7408_7_pin8));
  _7486 u_7486_3 (
    .pin1(n7408_1_pin1), .pin2(n7474_1_pin9), .pin3(n7486_3_pin3), .pin4(n7408_1_pin1), .pin5(n7474_1_pin9),
    .pin6(n7486_3_pin6));  // open: pin13, pin12, pin11, pin10, pin9, pin8
  _7408 u_7408_6 (
    .pin1(n7486_3_pin6), .pin2(n7408_5_pin6), .pin3(n7408_6_pin3));  // open: pin4, pin5, pin6, pin13, pin12, pin11, pin10, pin9, pin8
  _7404 u_7404_3 (
    .pin1(n7486_3_pin3), .pin3(n7408_6_pin3), .pin4(n7404_3_pin4));  // open: pin2, pin5, pin6, pin13, pin12, pin11, pin10, pin9, pin8
  _7408 u_7408_7 (
    .pin1(n7408_1_pin1), .pin2(n7408_1_pin2), .pin3(n7408_7_pin3), .pin4(n7408_1_pin4), .pin5(n7474_2_pin9),
    .pin6(n7408_7_pin6), .pin13(n7408_7_pin6), .pin12(n7408_1_pin12), .pin11(n7408_7_pin11),
    .pin10(n7408_7_pin6), .pin9(n7408_7_pin3), .pin8(n7408_7_pin8));
  _7486 u_7486_4 (
    .pin1(n7408_1_pin1), .pin2(n7474_1_pin9), .pin3(n7486_4_pin3), .pin4(n7408_1_pin1), .pin5(n7474_1_pin9),
    .pin6(n7486_4_pin6));  // open: pin13, pin12, pin11, pin10, pin9, pin8
  _7408 u_7408_8 (
    .pin1(n7486_4_pin6), .pin2(n7408_7_pin6), .pin3(n7408_8_pin3));  // open: pin4, pin5, pin6, pin13, pin12, pin11, pin10, pin9, pin8
  _7404 u_7404_4 (
    .pin1(n7486_4_pin3), .pin3(n7408_8_pin3), .pin4(n7404_4_pin4));  // open: pin2, pin5, pin6, pin13, pin12, pin11, pin10, pin9, pin8
  // also tied to VCC on the sheet: {n7474_1_pin1, n7474_2_pin1}
endmodule

module timer (
);

  wire and_1_out, and_2_out, and_3_out, and_4_out, and_5_out, and_6_out, and_7_out, and_8_out, and_9_out,
       and_10_out, and_11_out, and_12_out, and_13_out, and_14_out, and_15_out, and_16_out, and_17_out,
       and_18_out, clock_1_out, d_ff_1_q, d_ff_1_qn, d_ff_2_q, d_ff_2_qn, d_ff_3_q, d_ff_3_qn, d_ff_4_q,
       d_ff_4_qn, d_ff_5_q, d_ff_5_qn, not_1_out, not_2_out, not_3_out, not_4_out, not_5_out, not_6_out,
       not_7_out, not_8_out, not_9_out, not_10_out, not_11_out, not_12_out, not_13_out, not_14_out,
       not_15_out, not_16_out, not_17_out, not_18_out, not_19_out, not_20_out, not_21_out, not_22_out,
       not_23_out, not_24_out, not_25_out, not_26_out, not_27_out, not_28_out, not_29_out, not_30_out,
       not_31_out, not_32_out, not_33_out, not_34_out, not_35_out, not_36_out, not_37_out, not_38_out,
       not_39_out, not_40_out, not_41_out, not_42_out, not_43_out, not_44_out, or_1_out;

  Clock clock_1 (.out(clock_1_out));
  D_Flip_Flop d_ff_1 (.D(d_ff_1_qn), .clk(clock_1_out), .Q(d_ff_1_q), .Qn(d_ff_1_qn));  // open: preset, reset
  D_Flip_Flop d_ff_2 (.D(d_ff_2_qn), .clk(d_ff_1_qn), .Q(d_ff_2_q), .Qn(d_ff_2_qn));  // open: preset, reset
  D_Flip_Flop d_ff_3 (.D(d_ff_3_qn), .clk(d_ff_2_qn), .Q(d_ff_3_q), .Qn(d_ff_3_qn));  // open: preset, reset
  D_Flip_Flop d_ff_4 (.D(d_ff_4_qn), .clk(d_ff_3_qn), .Q(d_ff_4_q), .Qn(d_ff_4_qn));  // open: preset, reset
  D_Flip_Flop d_ff_5 (.D(d_ff_5_qn), .clk(d_ff_4_qn), .Q(d_ff_5_q), .Qn(d_ff_5_qn));  // open: preset, reset
  not not_1 (not_1_out, d_ff_2_q);
  not not_2 (not_2_out, d_ff_3_q);
  not not_3 (not_3_out, d_ff_4_q);
  not not_4 (not_4_out, d_ff_5_q);
  not not_5 (not_5_out, d_ff_1_q);
  not not_6 (not_6_out, d_ff_2_q);
  not not_7 (not_7_out, d_ff_4_q);
  not not_8 (not_8_out, d_ff_5_q);
  not not_9 (not_9_out, d_ff_1_q);
  not not_10 (not_10_out, d_ff_4_q);
  not not_11 (not_11_out, d_ff_5_q);
  not not_12 (not_12_out, d_ff_4_q);
  not not_13 (not_13_out, d_ff_5_q);
  not not_14 (not_14_out, d_ff_1_q);
  not not_15 (not_15_out, d_ff_3_q);
  not not_16 (not_16_out, d_ff_5_q);
  not not_17 (not_17_out, d_ff_2_q);
  not not_18 (not_18_out, d_ff_4_q);
  not not_19 (not_19_out, d_ff_1_q);
  not not_20 (not_20_out, d_ff_4_q);
  not not_21 (not_21_out, d_ff_5_q);
  not not_22 (not_22_out, d_ff_3_q);
  not not_23 (not_23_out, d_ff_5_q);
  not not_24 (not_24_out, d_ff_1_q);
  not not_25 (not_25_out, d_ff_2_q);
  not not_26 (not_26_out, d_ff_5_q);
  not not_27 (not_27_out, d_ff_1_q);
  not not_28 (not_28_out, d_ff_5_q);
  not not_29 (not_29_out, d_ff_1_q);
  not not_30 (not_30_out, d_ff_3_q);
  not not_31 (not_31_out, d_ff_4_q);
  not not_32 (not_32_out, d_ff_1_q);
  not not_33 (not_33_out, d_ff_2_q);
  not not_34 (not_34_out, d_ff_4_q);
  not not_35 (not_35_out, d_ff_2_q);
  not not_36 (not_36_out, d_ff_4_q);
  not not_37 (not_37_out, d_ff_1_q);
  not not_38 (not_38_out, d_ff_4_q);
  not not_39 (not_39_out, d_ff_2_q);
  not not_40 (not_40_out, d_ff_3_q);
  not not_41 (not_41_out, d_ff_1_q);
  not not_42 (not_42_out, d_ff_3_q);
  and and_1 (and_1_out, d_ff_1_q, not_1_out, not_2_out, not_3_out, not_4_out);
  and and_2 (and_2_out, not_5_out, not_6_out, d_ff_3_q, not_7_out, not_8_out);
  and and_3 (and_3_out, not_9_out, d_ff_2_q, d_ff_3_q, not_10_out, not_11_out);
  and and_4 (and_4_out, not_19_out, d_ff_2_q, d_ff_3_q, not_20_out, not_21_out);
  not not_43 (not_43_out, d_ff_3_q);
  not not_44 (not_44_out, d_ff_4_q);
  and and_5 (and_5_out, d_ff_1_q, d_ff_2_q, d_ff_3_q, not_12_out, not_13_out);
  and and_6 (and_6_out, not_14_out, d_ff_2_q, not_15_out, d_ff_4_q, not_16_out);
  and and_7 (and_7_out, d_ff_1_q, d_ff_2_q, not_22_out, d_ff_4_q, not_23_out);
  and and_8 (and_8_out, not_24_out, not_25_out, d_ff_3_q, d_ff_4_q, not_26_out);
  and and_9 (and_9_out, d_ff_1_q, not_17_out, d_ff_3_q, d_ff_5_q, not_18_out);
  and and_10 (and_10_out, not_27_out, d_ff_2_q, d_ff_3_q, d_ff_4_q, not_28_out);
  and and_11 (and_11_out, d_ff_1_q, d_ff_2_q, d_ff_3_q, d_ff_4_q, d_ff_5_q);
  and and_12 (and_12_out, not_29_out, d_ff_2_q, not_30_out, not_31_out, d_ff_5_q);
  and and_13 (and_13_out, d_ff_1_q, d_ff_2_q, not_43_out, not_44_out, d_ff_5_q);
  and and_14 (and_14_out, not_32_out, not_33_out, d_ff_3_q, not_34_out, d_ff_5_q);
  and and_15 (and_15_out, d_ff_1_q, not_35_out, d_ff_3_q, not_36_out, d_ff_5_q);
  and and_16 (and_16_out, not_37_out, d_ff_2_q, d_ff_3_q, not_38_out, d_ff_5_q);
  and and_17 (and_17_out, d_ff_1_q, not_39_out, not_40_out, d_ff_4_q, d_ff_5_q);
  and and_18 (and_18_out, not_41_out, d_ff_2_q, not_42_out, d_ff_4_q, d_ff_5_q);
  or or_1 (or_1_out, and_1_out, and_2_out, and_3_out, and_4_out, and_5_out, and_6_out, and_7_out, and_8_out, and_9_out, and_10_out, and_11_out, and_12_out, and_13_out, and_14_out, and_15_out, and_16_out, and_17_out, and_18_out);

  // Notes on the sheet:
  //   1.saniye
  //   4.saniye
  //   5.saniye
  //   6..saniye
  //   7.saniye
  //   10.saniye
  //   11.saniye
  //   12.saniye
  //   13.saniye
  //   14.saniye
  //   15.saniye
  //   18.saniye
  //   19.saniye
  //   20.saniye
  //   21.saniye
  //   22.saniye
  //   25.saniye
  //   26.saniye
endmodule
